// Logisim project FPGA.circ as structural Verilog: 2 circuits, main circuit FPGA_G3-G4
module FPGA_G3_G4 (
  input  E0,
  input  E1
);

  wire not_1_out, undriven;

  nor nor_1 (E0, not_1_out, undriven);
  and and_1 (E1, not_1_out, undriven);
  not not_1 (not_1_out, undriven);
  Clock CLK ();  // open: out
endmodule

module FPGA_G1_G2 (
  input  BTN2,
  input  BTN2_2,
  output G2,
  output G1,
  output BTN2_2NEG,
  output BTN2_NEG,
  output G2_2,
  output G1_2,
  output BTN2_2NEG_2,
  output BTN2_NEG_2
);

  nor nor_1 (G2, BTN2_2NEG, BTN2_NEG);
  and and_1 (G1, BTN2_NEG, BTN2_2NEG);
  nor nor_2 (G2_2, 1'b0, 1'b0);
  and and_2 (G1_2, 1'b0, 1'b0);
  not not_1 (BTN2_2NEG, BTN2_NEG);
  // NOT_Gate not_2 has open pins: in=1'b0, out=open
  not not_3 (BTN2_NEG, BTN2);
  // NOT_Gate not_4 has open pins: in=BTN2_2, out=open

  assign BTN2_2NEG_2 = 1'b0;
  assign BTN2_NEG_2 = 1'b0;

  // Notes on the sheet:
  //   Das zweite Schaltbild dient der Simulation der Verzögerung der Inverter. Hierzu können die Konstanten unabhängig voneinander mit 0x0 und 0x1 verwendet werden.
endmodule
