// Logisim project schaltwerk.circ as structural Verilog: 1 circuit, main circuit main
module main (
  input  q0,
  input  q1,
  input  BTN0_prime,
  input  BTN1_prime,
  output q0_prime,
  output q1_prime
);

  wire and_1_out, and_2_out, and_3_out, and_4_out, and_5_out, and_6_out, clock_1_out, or_1_out, or_2_out;

  and and_1 (and_1_out, q0, ~q1, ~BTN0_prime);  // AND_Gate
  and and_2 (and_2_out, ~q0, ~q1, BTN0_prime, ~BTN1_prime);  // AND_Gate
  and and_3 (and_3_out, ~q1, q0, BTN0_prime, BTN1_prime);  // AND_Gate
  and and_4 (and_4_out, ~q1, ~BTN0_prime, BTN1_prime, ~q0);  // AND_Gate
  and and_5 (and_5_out, BTN1_prime, BTN0_prime, q1, ~q0);  // AND_Gate
  and and_6 (and_6_out, ~BTN1_prime, q1, ~q0);  // AND_Gate
  or or_1 (or_1_out, and_1_out, and_2_out, and_3_out);
  or or_2 (or_2_out, and_4_out, and_5_out, and_6_out);
  Clock clock_1 (.out(clock_1_out));
  D_Flip_Flop d_ff_1 (.clk(clock_1_out), .D(or_1_out), .Q(q0_prime));  // open: Qn, preset, en, reset
  D_Flip_Flop d_ff_2 (.clk(clock_1_out), .D(or_2_out), .Q(q1_prime));  // open: Qn, preset, en, reset
endmodule
